# Fritzing sketch photoresistor (saved by Fritzing 0.9.2b)
breadboards: 1

parts:
  Static_Resistor = Resistor [tolerance=±5% resistance=10k package=THT]
  Photoresistor = Photocell (LDR) [package=THT]
  Voltage_Divider = Arduino Uno (Rev3)

nets:
  N1: Static_Resistor.Pin_0, Photoresistor.pin_1, Voltage_Divider.A0
  N2: Static_Resistor.Pin_1, Voltage_Divider.3V3
  N3: Photoresistor.pin_0, Voltage_Divider.GND
