# Fritzing sketch photon_lab02 (saved by Fritzing 0.9.2b)
breadboards: 1

parts:
  Photon = Photon
  R3 = Resistor [tolerance=±5% resistance=220 package=THT]
  Photoresistor = Photocell (LDR) [package=THT]

nets:
  N1: Photon.A0, R3.Pin_0, Photoresistor.pin_0
  N2: Photon.GND, Photoresistor.pin_1
  N3: Photon.3V3, R3.Pin_1
