# Fritzing sketch photon_lab01_bb (saved by Fritzing 0.9.2b)
breadboards: 1

parts:
  Part1 = Photon
  R1 = Resistor [tolerance=±5% resistance=220 package=THT]
  LED1 = LED - 3mm [color="Red (633nm)" package="3 mm [THT]"]
  R3 = Resistor [tolerance=±5% resistance=220 package=THT]
  R2 = Photocell (LDR) [package=THT]

nets:
  N1: Part1.A0, R3.Pin_0, R2.pin_0
  N2: Part1.GND, R1.Pin_1, R2.pin_1
  N3: Part1.D7, LED1.anode
  N4: Part1.3V3, R3.Pin_1
  N5: R1.Pin_0, LED1.cathode
