# Fritzing sketch photon_lightsensor (saved by Fritzing 0.9.2b)
breadboards: 1

parts:
  Part1 = Photon
  R3 = Resistor [tolerance=±5% resistance=220 package=THT]
  R2 = Photocell (LDR) [package=THT]
  LED1 = LED - 5mm [color="Red (633nm)" package="5 mm [THT]"]
  R4 = Resistor [tolerance=±5% resistance=10k package=THT]

nets:
  N1: Part1.A0, R3.Pin_0, R2.pin_0
  N2: Part1.GND, R2.pin_1, R4.Pin_1
  N3: Part1.D0, LED1.anode
  N4: Part1.3V3, R3.Pin_1
  N5: LED1.cathode, R4.Pin_0
