# Fritzing sketch photon_tmp36_bb (saved by Fritzing 0.9.2b)
breadboards: 1

parts:
  Part1 = Photon
  T1 = TMP36 Temperature Sensor [package="TO92 [THT]"]

nets:
  N1: Part1.A0, T1.Vout
  GND: Part1.GND, T1.GND
  N2: Part1.3V3, T1.+Vs
