# Fritzing sketch rpi2_hello_windows (saved by Fritzing 0.9.2b)
breadboards: 1

parts:
  Raspberry_Pi1 = Raspberry Pi 2
  R1 = Resistor [tolerance=±5% resistance=330 package=THT]
  LED1 = LED - 5mm [color="Red (633nm)" package="5 mm [THT]"]

nets (from the schematic view):
  N1: Raspberry_Pi1.GND, R1.Pin_0
  N2: Raspberry_Pi1.GPIO12, LED1.anode
  N3: R1.Pin_1, LED1.cathode
