# Fritzing sketch rpi2_IoTLightSensor_mcp3008 (saved by Fritzing 0.9.2b)
breadboards: 1

parts:
  Raspberry_Pi1 = Raspberry Pi 2
  R1 = Resistor [tolerance=±5% resistance=330 package=THT]
  LED1 = LED - 5mm [color="Red (633nm)" package="5 mm [THT]"]
  R2 = Photocell (LDR) [package=THT]
  R3 = Resistor [tolerance=±5% resistance=10k package=THT]
  IC1 = MCP3008 8-channel 10-bit ADC [part_number=MCP3008]

nets (from the breadboard view):
  N1: Raspberry_Pi1.GPIO10, IC1.no_name_yet#11
  N2: Raspberry_Pi1.GPIO9, IC1.no_name_yet#12
  N3: Raspberry_Pi1.GPIO11, IC1.no_name_yet#13
  N4: Raspberry_Pi1.GND, R1.Pin_1, R2.pin_1, IC1.no_name_yet#9, IC1.no_name_yet#14
  N5: Raspberry_Pi1.GPIO12, LED1.anode
  N6: Raspberry_Pi1.GPIO8, IC1.no_name_yet#10
  N7: Raspberry_Pi1.5V, R3.Pin_0, IC1.no_name_yet#15, IC1.no_name_yet#16
  N8: R1.Pin_0, LED1.cathode
  N9: R2.pin_0, R3.Pin_1, IC1.no_name_yet#1
