# Fritzing sketch rpi2_lab03 (saved by Fritzing 0.9.2b)
breadboards: 1

parts:
  Raspberry_Pi1 = Raspberry Pi 2
  R1 = Resistor [tolerance=±5% resistance=330 package=THT]
  MCP3003 = IC, DIP package, 8 pins [chip_label=MCP3002]
  LED1 = LED - 5mm [color="Red (633nm)" package="5 mm [THT]"]
  R2 = Photocell (LDR) [package=THT]
  R3 = Resistor [tolerance=±5% resistance=10k package=THT]

nets (from the breadboard view):
  N1: Raspberry_Pi1.3v3, MCP3003.pin8, R3.Pin_0
  N2: Raspberry_Pi1.GPIO10, MCP3003.pin5
  N3: Raspberry_Pi1.GPIO9, MCP3003.pin6
  N4: Raspberry_Pi1.GPIO11, MCP3003.pin7
  N5: Raspberry_Pi1.GND, R1.Pin_0, MCP3003.pin4, R2.pin_1
  N6: Raspberry_Pi1.GPIO12, LED1.anode
  N7: R1.Pin_1, LED1.cathode
  N8: MCP3003.pin3, R2.pin_0, R3.Pin_1
